# Fritzing sketch sensor (saved by Fritzing 0.9.0b)
circuit board: 2.2cm x 5.5cm
breadboards: 1

parts:
  R1 = Resistor [tolerance=±5% resistance=220 package=THT]
  LED4 = LED - 5mm [color="Red (633nm)" package="5 mm [THT]"]
  LED5 = LED - 5mm [color="Red (633nm)" package="5 mm [THT]"]
  LED6 = LED - 5mm [color="Red (633nm)" package="5 mm [THT]"]
  R2 = Resistor [tolerance=±5% resistance=220 package=THT]
  R3 = Resistor [tolerance=±5% resistance=220 package=THT]
  R4 = Resistor [tolerance=±5% resistance=220 package=THT]
  J1 = female pin header, 5 pins [form="♀ (female)"]
  part = female pin header, 5 pins [form="♀ (female)"]  # not connected
  LED7 = LED - 5mm [color="Blue (430nm)" package="5 mm [THT]"]
  LED1 = LED - 5mm [color="Blue (430nm)" package="5 mm [THT]"]
  LED2 = LED - 5mm [color="Blue (430nm)" package="5 mm [THT]"]
  LED3 = LED - 5mm [color="Blue (430nm)" package="5 mm [THT]"]

nets:
  N1: R1.Pin_0, LED4.anode, LED5.anode, LED6.anode, J1.pin5
  N2: R1.Pin_1, LED7.anode, LED1.anode, LED2.anode, LED3.anode
  N3: LED4.cathode, R2.Pin_0, J1.pin2
  N4: LED5.cathode, R3.Pin_0, J1.pin3
  N5: LED6.cathode, R4.Pin_0, J1.pin4
  GND: R2.Pin_1, R3.Pin_1, R4.Pin_1, J1.pin1, LED7.cathode, LED1.cathode, LED2.cathode, LED3.cathode
